// Logisim project main_cpu.circ as structural Verilog: 1 circuit, main circuit CPU
module CPU (
);

  wire AE, and_2_out, and_3_out, and_4_out, and_6_out, and_8_out, and_15_out, and_17_out, AS, clock_1_out,
       DA, demultiplexer_1_out0, demultiplexer_1_out1, demultiplexer_1_out2, demultiplexer_1_out3, GC, I5J,
       IA, LOOP_ACTIVE_q, M, n74193_1_pin1, n74193_1_pin4, n74193_1_pin15, not_1_out, not_2_out, not_3_out,
       not_4_out, not_5_out, not_6_out, not_7_out, not_8_out, not_9_out, not_10_out, not_13_out, or_6_out,
       or_7_out, register_1_q, RLD, RST;
  wire [1:0] and_9_out, demultiplexer_3_out0, demultiplexer_3_out1, n74193_1_pin3, n74193_1_pin6;
  wire [2:0] and_13_out, IR_q, IR_q_3, LC_q, multiplexer_5_out, not_12_out, register_2_q, subtractor_2_out;
  wire [2:2] or_2_out;
  wire [4:3] IR_q_2;
  wire [7:0] ACC_q, adder_1_out, adder_2_out, adder_3_out, and_10_out, demultiplexer_2_out0,
       demultiplexer_2_out1, demultiplexer_2_out2, demultiplexer_2_out3, divider_1_out, divider_1_rem, MAR_q,
       multiplexer_1_out, multiplexer_2_out, multiplexer_3_out, multiplexer_4_out, multiplexer_6_out,
       multiplier_1_out, or_4_out, PC_q, ram_1_dout, REGA_q, REGB_q, rom_1_data, subtractor_1_out, xor_1_out;

  and and_1 (AS, M, DA);
  or or_1 (AE, AS, IA);
  and and_2 (and_2_out, IR_q[2], not_9_out);
  Register #(.trigger("falling"), .width(1)) register_1 (
    .D(and_6_out), .clk(clock_1_out), .Q(register_1_q));  // open: en, clr
  or or_2 (or_2_out[2], and_3_out, and_2_out);
  or or_3 (and_9_out[1], and_4_out, and_8_out);
  and and_3 (and_3_out, IA, IR_q_3[1]);
  and and_4 (and_4_out, IA, IR_q_3[2]);
  ROM rom_1 (.addr(multiplexer_6_out), .data(rom_1_data));
  Clock clock_1 (.out(clock_1_out));
  and and_5 (GC, clock_1_out, not_1_out);
  not not_1 (not_1_out, register_1_q);
  not not_2 (not_2_out, IR_q_3[1]);
  not not_3 (not_3_out, IR_q_3[0]);
  not not_4 (not_4_out, IR_q_2[4]);
  and and_6 (and_6_out, IR_q_3[2], not_2_out, not_3_out, not_4_out, not_5_out, not_6_out, not_7_out, not_8_out);
  not not_5 (not_5_out, IR_q_2[3]);
  not not_6 (not_6_out, IR_q[2]);
  not not_7 (not_7_out, IR_q[1]);
  not not_8 (not_8_out, IR_q[0]);
  Register REGA (.D(demultiplexer_2_out1), .en(demultiplexer_1_out1), .clk(GC), .Q(REGA_q));  // open: clr
  Register REGB (.D(demultiplexer_2_out0), .en(demultiplexer_1_out0), .clk(GC), .Q(REGB_q));  // open: clr
  and and_7 (DA, and_8_out, and_9_out[0]);
  and and_8 (and_8_out, IR_q[1], not_9_out);
  and and_9 (and_9_out[0], IR_q[0], not_9_out);
  Register IR (.D(rom_1_data), .clk(GC), .Q({IR_q_3, IR_q_2, IR_q}));  // open: en, clr
  Adder adder_1 (.a(REGA_q), .b(REGB_q), .out(adder_1_out));  // open: cin, cout
  Subtractor subtractor_1 (.a(REGA_q), .b(REGB_q), .out(subtractor_1_out));  // open: bin, bout
  Multiplier multiplier_1 (.a(REGA_q), .b(REGB_q), .out(multiplier_1_out));  // open: cin, cout
  Divider divider_1 (.a(REGA_q), .b(REGB_q), .out(divider_1_out), .rem(divider_1_rem));  // open: upper
  assign and_10_out = REGA_q & REGB_q;  // AND_Gate and_10, 8 bits wide
  assign or_4_out = REGA_q | REGB_q;  // OR_Gate or_4, 8 bits wide
  assign xor_1_out = REGA_q ^ REGB_q;  // XOR_Gate xor_1, 8 bits wide
  not not_9 (not_9_out, IA);
  nor nor_1 (IA, IR_q_3[0], IR_q_2[4], IR_q_2[3]);
  and and_11 (and_13_out[2], IA, IR_q[2]);
  not not_10 (not_10_out, GC);
  and and_12 (and_13_out[1], IA, IR_q[1]);
  and and_13 (and_13_out[0], IA, IR_q[0]);
  Register MAR (.D(demultiplexer_2_out2), .en(demultiplexer_1_out2), .clk(GC), .Q(MAR_q));  // open: clr
  Register ACC (.D(multiplexer_2_out), .en(AE), .clk(GC), .Q(ACC_q));  // open: clr
  // Probe on multiplexer_1_out
  Multiplexer #(.select(3), .width(8)) multiplexer_1 (
    .in0(adder_1_out), .in1(subtractor_1_out), .in2(multiplier_1_out), .in3(divider_1_out),
    .in4(divider_1_rem), .in5(and_10_out), .in6(or_4_out), .in7(xor_1_out), .out(multiplexer_1_out),
    .sel(register_2_q));
  Multiplexer #(.width(8)) multiplexer_2 (
    .in0(multiplexer_1_out), .in1(demultiplexer_2_out3), .out(multiplexer_2_out), .sel(AS));
  Register #(.trigger("falling"), .width(3)) register_2 (
    .D(and_13_out), .en(IA), .clk(clock_1_out), .Q(register_2_q));  // open: clr
  _74193 u_74193_1 (
    .pin1(n74193_1_pin1), .pin2(n74193_1_pin3[1]), .pin3(n74193_1_pin3[0]), .pin4(n74193_1_pin4), .pin5(IA),
    .pin6(n74193_1_pin6[0]), .pin7(n74193_1_pin6[1]), .pin15(n74193_1_pin15), .pin11(not_10_out),
    .pin10(n74193_1_pin1), .pin9(n74193_1_pin1));  // open: pin14, pin13, pin12
  Register #(.width(3)) LC (.D(subtractor_2_out), .en(and_17_out), .clk(GC), .Q(LC_q));  // open: clr
  Subtractor #(.width(3)) subtractor_2 (.a(multiplexer_5_out), .b(3'b001), .out(subtractor_2_out));  // open: bin, bout
  RAM ram_1 (.addr(MAR_q), .we(RST), .oe(RLD), .clk(GC), .din(ACC_q), .dout(ram_1_dout));
  or or_5 (M, I5J, IA);
  // Probe on ACC_q
  or or_6 (or_6_out, n74193_1_pin6[1], n74193_1_pin6[0], n74193_1_pin3[1], n74193_1_pin3[0]);
  and and_14 (n74193_1_pin4, or_6_out, GC);
  Button #(.press("passive")) button_1 (.out(n74193_1_pin15));
  and and_15 (and_15_out, and_17_out, or_7_out);
  Multiplexer #(.enable("true"), .select(2), .width(8)) multiplexer_3 (
    .in0(REGB_q), .in1(REGA_q), .in2(MAR_q), .in3(ram_1_dout), .out(multiplexer_3_out),
    .sel(demultiplexer_3_out0), .en(M));
  // AND_Gate and_16 has open pins: in0=demultiplexer_1_out3, in1=GC, out=open
  // NOT_Gate not_11 has open pins: in=or_6_out, out=open
  assign not_12_out = ~IR_q;  // NOT_Gate not_12, 3 bits wide
  Register #(.width(1)) LOOP_ACTIVE (.D(and_15_out), .en(and_17_out), .clk(GC), .Q(LOOP_ACTIVE_q));  // open: clr
  Demultiplexer #(.enable("true"), .select(2)) demultiplexer_1 (
    .out0(demultiplexer_1_out0), .out1(demultiplexer_1_out1), .out2(demultiplexer_1_out2),
    .out3(demultiplexer_1_out3), .in(M), .sel(and_9_out), .en(M));
  Demultiplexer #(.enable("true"), .select(2), .width(8)) demultiplexer_2 (
    .out0(demultiplexer_2_out0), .out1(demultiplexer_2_out1), .out2(demultiplexer_2_out2),
    .out3(demultiplexer_2_out3), .in(multiplexer_4_out), .sel(and_9_out), .en(M));
  Multiplexer #(.width(8)) multiplexer_4 (
    .in0(multiplexer_3_out), .in1({{6{1'b0}}, demultiplexer_3_out1}), .out(multiplexer_4_out),
    .sel(or_2_out[2]));
  Demultiplexer #(.width(2)) demultiplexer_3 (
    .out0(demultiplexer_3_out0), .out1(demultiplexer_3_out1), .in(IR_q_3[2:1]), .sel(or_2_out[2]));
  and and_17 (and_17_out, IR_q_2[3], IR_q_2[4]);
  not not_13 (not_13_out, and_17_out);
  or or_7 (or_7_out, multiplexer_5_out[0], multiplexer_5_out[1], multiplexer_5_out[2]);
  Multiplexer #(.width(3)) multiplexer_5 (.in0(IR_q_3), .in1(LC_q), .out(multiplexer_5_out), .sel(LOOP_ACTIVE_q));
  // Probe on ram_1_dout
  Multiplexer #(.width(8)) multiplexer_6 (.in0(PC_q), .in1(adder_2_out), .out(multiplexer_6_out), .sel(and_15_out));
  Adder adder_2 (.a(PC_q), .b({{5{1'b1}}, not_12_out}), .out(adder_2_out));  // open: cin, cout
  and and_18 (RST, IR_q_2[3], not_13_out);
  and and_19 (RLD, IR_q_2[4], not_13_out);
  and and_20 (I5J, IR_q_3[0], not_13_out);
  Register PC (.D(adder_3_out), .clk(GC), .Q(PC_q));  // open: en, clr
  Adder adder_3 (.a(multiplexer_6_out), .b(8'h1), .out(adder_3_out));  // open: cin, cout
  // also tied to GND on the sheet: n74193_1_pin1

  // Notes on the sheet:
  //   contents of rom_1 (hex, n*v repeats v):
  //   e5 64 26 0 8 66 65 24 0 8 10 e0 a6 0 8 a5 a4 26 10 e2 0 8 26 10 e1 64 0 8 a5 10 e2 0 8 26 10 e1 0 8
  //   10 e1 0 8 a5 10 e2 0 8 26 10 e1 0 8 10 e2 a5 a4 0 8 64 26 26 10 e1 a4 0 8 64 10 e2 65 0 8 26 10 e1 0
  //   8 10 e2 65 2 8 26 10 e1 a4 0 8 a5 e6 0 8 66 10 e1 e6 10 e2 10 e0 26 10 e2 0 8 64 e6 10 e1 0 8 26 10
  //   e1 0 8 a6 10 e1 e6 10 e2 10 e0 26 10 e2 0 8 26 e4 10 e1 0 8 10 e1 a4 0 8 e6 10 e1 0 8 10 e1 e2 e4 0
  //   10 e6 8 e1 10 e2 10 e0 26 10 e2 0 8 26 64 e1 0 8 e6 10 e1 0 8 a4 10 1 8 e2 10 e1 e6 10 e2 10 e0 26
  //   10 e2 0 8 25 24 26 0 8 e6 8 26 80 80
endmodule
